# Fritzing sketch circuito (saved by Fritzing 0.9.3b)
breadboards: 1

parts:
  U1 = NodeMCU V1.0
  Part1 = RFID-RC522-v2
  LED1 = LED - 3mm [color="Red (633nm)" package="3 mm [THT]"]
  LED2 = LED - 3mm [color="Green (570nm)" package="3 mm [THT]"]
  R1 = Resistor [tolerance=±5% resistance=220 package=THT]
  R2 = Resistor [tolerance=±5% resistance=220 package=THT]
  J1 = Piezo Speaker

nets:
  N1: U1.D0, R1.Pin_0
  N2: U1.D1, Part1.RST
  N3: U1.D2, Part1.SDA
  N4: U1.D3, R2.Pin_0
  N5: U1.D4, J1.pin2
  GND: U1.GND, Part1.GND, LED1.anode, LED2.anode, J1.pin1
  N6: U1.D5, Part1.SCK
  N7: U1.D6, Part1.MISO
  N8: U1.D7, Part1.MOSI
  3V3: U1.3V3, Part1.3.3V
  N9: LED1.cathode, R1.Pin_1
  N10: LED2.cathode, R2.Pin_1

custom parts:
  NodeMCU V1.0: ESP8266 based NodeMCU
  RFID-RC522-v2: A simple China made RFID-RC522 Reader; do check the pin labels, as this is a MFRC522 based clone.
